// Logisim project MIC-1.circ as structural Verilog
module main (
  input  CLK,
  output [31:0] PC,
  output [8:0] MPC,
  output [31:0] B,
  output [31:0] C
);

  wire control_unit_1_cpp_b, control_unit_1_cpp_c, control_unit_1_h_c, control_unit_1_lv_b,
       control_unit_1_lv_c, control_unit_1_mar_c, control_unit_1_mbr_b, control_unit_1_mbru_b,
       control_unit_1_mdr_b, control_unit_1_mdr_c, control_unit_1_opc_b, control_unit_1_opc_c,
       control_unit_1_pc_b, control_unit_1_pc_c, control_unit_1_sp_b, control_unit_1_sp_c,
       control_unit_1_tos_b, control_unit_1_tos_c, data_path_1_n, data_path_1_z, RESET_out;
  wire [1:0] control_unit_1_alu_2, control_unit_1_shifter;
  wire [2:0] control_unit_1_mem;
  wire [3:0] control_unit_1_alu;
  wire [7:0] data_path_1_op_code, mem_1_mem_fetch;
  wire [31:0] data_path_1_mem_mar, data_path_1_mem_wr, mem_1_mrm_rd;

  Mem mem_1 (
    .MEM_ADDR_32(data_path_1_mem_mar), .CLK(CLK), .MEM_WR(data_path_1_mem_wr), .MRM_RD(mem_1_mrm_rd),
    .MEM_FETCH(mem_1_mem_fetch), .wr(control_unit_1_mem[2]), .rd(control_unit_1_mem[1]),
    .fetch(control_unit_1_mem[0]), .MEM_ADDR_8(PC));
  Button RESET (.out(RESET_out));
  Data_Path data_path_1 (
    .MEM_WR(data_path_1_mem_wr), .MEM_RD(mem_1_mrm_rd), .rd(control_unit_1_mem[1]),
    .MEM_FETCH(mem_1_mem_fetch), .RESET(RESET_out), .INVA(control_unit_1_alu[1]),
    .ENA(control_unit_1_alu[3]), .CLK(CLK), .ENB(control_unit_1_alu[2]), .INC(control_unit_1_alu[0]),
    .F(control_unit_1_alu_2), .SRA1(control_unit_1_shifter[0]), .SLL8(control_unit_1_shifter[1]),
    .MEM_MAR(data_path_1_mem_mar), .OP_CODE(data_path_1_op_code), .N(data_path_1_n), .Z(data_path_1_z),
    .MAR_C(control_unit_1_mar_c), .MDR_C(control_unit_1_mdr_c), .PC_C(control_unit_1_pc_c),
    .fetch(control_unit_1_mem[0]), .SP_C(control_unit_1_sp_c), .LV_C(control_unit_1_lv_c),
    .CPP_C(control_unit_1_cpp_c), .TOS_C(control_unit_1_tos_c), .OPC_C(control_unit_1_opc_c),
    .H_C(control_unit_1_h_c), .MBR(control_unit_1_mbr_b), .MBRU(control_unit_1_mbru_b),
    .MDR_B(control_unit_1_mdr_b), .PC_B(control_unit_1_pc_b), .SP_B(control_unit_1_sp_b),
    .LV_B(control_unit_1_lv_b), .CPP_B(control_unit_1_cpp_b), .TOS_B(control_unit_1_tos_b),
    .OPC_B(control_unit_1_opc_b), .MEM_PC(PC), .B(B), .C(C));
  Control_Unit control_unit_1 (
    .CLK(CLK), .RESET(RESET_out), .MBR(data_path_1_op_code), .N(data_path_1_n), .Z(data_path_1_z), .MPC(MPC),
    .MDR_B(control_unit_1_mdr_b), .PC_B(control_unit_1_pc_b), .MBR_B(control_unit_1_mbr_b),
    .MBRU_B(control_unit_1_mbru_b), .SP_B(control_unit_1_sp_b), .LV_B(control_unit_1_lv_b),
    .CPP_B(control_unit_1_cpp_b), .TOS_B(control_unit_1_tos_b), .OPC_B(control_unit_1_opc_b),
    .Mem(control_unit_1_mem), .ALU({control_unit_1_alu_2, control_unit_1_alu}),
    .Shifter(control_unit_1_shifter), .H_C(control_unit_1_h_c), .OPC_C(control_unit_1_opc_c),
    .TOS_C(control_unit_1_tos_c), .CPP_C(control_unit_1_cpp_c), .LV_C(control_unit_1_lv_c),
    .SP_C(control_unit_1_sp_c), .PC_C(control_unit_1_pc_c), .MDR_C(control_unit_1_mdr_c),
    .MAR_C(control_unit_1_mar_c));
endmodule

module Mem (
  input  wr,
  input  [31:0] MEM_WR,
  input  [31:0] MEM_ADDR_32,
  input  rd,
  input  [31:0] MEM_ADDR_8,
  input  fetch,
  input  CLK,
  output [31:0] MRM_RD,
  output [7:0] MEM_FETCH
);

  wire not_1_out, not_2_out, not_3_out;
  wire [7:0] ram_2_data;
  wire [31:0] ram_1_data;

  not not_1 (not_1_out, CLK);
  not not_2 (not_2_out, wr);
  RAM #(.addrWidth(24), .dataWidth(32)) ram_1 (
    .addr(MEM_ADDR_32[23:0]), .data(ram_1_data), .sel(1'b1), .clk(not_1_out), .ld(not_2_out), .clr(1'b0));
  assign ram_1_data = wr ? MEM_WR : 32'bz;  // Controlled_Buffer controlled_buffer_1
  assign MRM_RD = rd ? ram_1_data : 32'bz;  // Controlled_Buffer controlled_buffer_2
  not not_3 (not_3_out, CLK);
  assign MEM_FETCH = fetch ? ram_2_data : 8'bz;  // Controlled_Buffer controlled_buffer_3
  RAM #(.addrWidth(24)) ram_2 (
    .addr(MEM_ADDR_8[23:0]), .data(ram_2_data), .sel(1'b1), .clk(not_3_out), .clr(1'b0));  // open: ld

  // Notes on the sheet:
  //   Una truchada porque Logisim no tiene
  //   un bloque de memoria con dos canales de datos
endmodule

module Control_Unit (
  input  CLK,
  input  RESET,
  input  [7:0] MBR,
  input  N,
  input  Z,
  output [8:0] MPC,
  output MDR_B,
  output PC_B,
  output MBR_B,
  output MBRU_B,
  output SP_B,
  output LV_B,
  output CPP_B,
  output TOS_B,
  output OPC_B,
  output [2:0] Mem,
  output [5:0] ALU,
  output [1:0] Shifter,
  output H_C,
  output OPC_C,
  output TOS_C,
  output CPP_C,
  output LV_C,
  output SP_C,
  output PC_C,
  output MDR_C,
  output MAR_C
);

  wire and_1_out, and_2_out, d_flipflop_asc_1_q, d_flipflop_asc_2_q, not_1_out;
  wire [2:0] mir_1_jam;
  wire [3:0] control_store_1_cs_s4, mir_1_b;
  wire [7:0] mir_1_addr, multiplexer_3_out, or_2_out;
  wire [8:0] multiplexer_1_out, multiplexer_2_out;
  wire [8:8] mir_1_addr_2, or_1_out;
  wire [31:0] control_store_1_cs_s32;

  Multiplexer #(.width(9), .enable("false")) multiplexer_1 (
    .in0({9{1'b1}}), .in1(9'hff), .out(multiplexer_1_out), .sel(RESET));
  Multiplexer #(.width(9), .enable("false")) multiplexer_2 (
    .in0({9{1'b1}}), .in1(9'h100), .out(multiplexer_2_out), .sel(RESET));
  and and_1 (and_1_out, d_flipflop_asc_1_q, mir_1_jam[1]);
  D_FlipFlop_Asc d_flipflop_asc_1 (
    .D(N), .CLK(CLK), .Q(d_flipflop_asc_1_q), .nPRE(1'b1), .nCLR(not_1_out));  // open: nQ
  D_FlipFlop_Asc d_flipflop_asc_2 (
    .D(Z), .CLK(CLK), .Q(d_flipflop_asc_2_q), .nPRE(1'b1), .nCLR(not_1_out));  // open: nQ
  Multiplexer #(.width(8), .enable("false")) multiplexer_3 (
    .in0(mir_1_addr), .in1(or_2_out), .out(multiplexer_3_out), .sel(mir_1_jam[2]));
  or or_1 (or_1_out[8], and_1_out, and_2_out, mir_1_addr_2[8]);
  and and_2 (and_2_out, d_flipflop_asc_2_q, mir_1_jam[0]);
  assign or_2_out = MBR | mir_1_addr;  // OR_Gate or_2, 8 bits wide
  not not_1 (not_1_out, RESET);
  MPC mpc_1 (
    .Entrada({or_1_out[8], multiplexer_3_out}), .CLK(CLK), .Salida(MPC), .nPRE(multiplexer_1_out),
    .nCLR(multiplexer_2_out));
  Control_Store control_store_1 (.CS_E(MPC), .CS_S32(control_store_1_cs_s32), .CS_S4(control_store_1_cs_s4));
  MIR mir_1 (
    .Entrada_4(control_store_1_cs_s4), .Entrada_32(control_store_1_cs_s32), .CLK(CLK), .RESET(RESET),
    .B(mir_1_b), .Mem(Mem), .C({H_C, OPC_C, TOS_C, CPP_C, LV_C, SP_C, PC_C, MDR_C, MAR_C}),
    .ALU({Shifter, ALU}), .JAM(mir_1_jam), .Addr({mir_1_addr_2[8], mir_1_addr}));
  Decoder_part #(.select(4), .enable("false")) decoder_1 (
    .out0(MDR_B), .out1(PC_B), .out2(MBR_B), .out3(MBRU_B), .out4(SP_B), .out5(LV_B), .out6(CPP_B),
    .out7(TOS_B), .out8(OPC_B), .sel(mir_1_b));  // open: out9, out10, out11, out12, out13, out14, out15
endmodule

module Control_Store (
  input  [8:0] CS_E,
  output [31:0] CS_S32,
  output [3:0] CS_S4
);

  ROM #(.addrWidth(9), .dataWidth(32)) rom_1 (.addr(CS_E), .data(CS_S32), .sel(1'b1));
  ROM #(.addrWidth(9), .dataWidth(4)) rom_2 (.addr(CS_E), .data(CS_S4), .sel(1'b1));

  // Notes on the sheet:
  //   Otra truchada porque Logisim no tiene
  //   un bloque de memoria mas ancho que 32 bits
  //   contents of rom_1 (hex, n*v repeats v):
  //   80000000 255*0 435021
  //   contents of rom_2 (hex, n*v repeats v):
  //   f 255*0 1
endmodule

module MPC (
  input  [8:0] nPRE,
  input  [8:0] Entrada,
  input  CLK,
  input  [8:0] nCLR,
  output [8:0] Salida
);

  D_Latch d_latch_1 (.D(Entrada[8]), .CLK(CLK), .Q(Salida[8]), .nPRE(nPRE[8]), .nCLR(nCLR[8]));  // open: nQ
  D_Latch d_latch_2 (.D(Entrada[7]), .CLK(CLK), .Q(Salida[7]), .nPRE(nPRE[7]), .nCLR(nCLR[7]));  // open: nQ
  D_Latch d_latch_3 (.D(Entrada[6]), .CLK(CLK), .Q(Salida[6]), .nPRE(nPRE[6]), .nCLR(nCLR[6]));  // open: nQ
  D_Latch d_latch_4 (.D(Entrada[5]), .CLK(CLK), .Q(Salida[5]), .nPRE(nPRE[5]), .nCLR(nCLR[5]));  // open: nQ
  D_Latch d_latch_5 (.D(Entrada[4]), .CLK(CLK), .Q(Salida[4]), .nPRE(nPRE[4]), .nCLR(nCLR[4]));  // open: nQ
  D_Latch d_latch_6 (.D(Entrada[3]), .CLK(CLK), .Q(Salida[3]), .nPRE(nPRE[3]), .nCLR(nCLR[3]));  // open: nQ
  D_Latch d_latch_7 (.D(Entrada[2]), .CLK(CLK), .Q(Salida[2]), .nPRE(nPRE[2]), .nCLR(nCLR[2]));  // open: nQ
  D_Latch d_latch_8 (.D(Entrada[1]), .CLK(CLK), .Q(Salida[1]), .nPRE(nPRE[1]), .nCLR(nCLR[1]));  // open: nQ
  D_Latch d_latch_9 (.D(Entrada[0]), .CLK(CLK), .Q(Salida[0]), .nPRE(nPRE[0]), .nCLR(nCLR[0]));  // open: nQ
endmodule

module MIR (
  input  [3:0] Entrada_4,
  input  [31:0] Entrada_32,
  input  CLK,
  input  RESET,
  output [3:0] B,
  output [2:0] Mem,
  output [8:0] C,
  output [7:0] ALU,
  output [2:0] JAM,
  output [8:0] Addr
);

  wire [3:0] multiplexer_2_out, multiplexer_4_out, not_2_out;
  wire [31:0] multiplexer_1_out, multiplexer_3_out, not_1_out;

  Multiplexer #(.width(32), .enable("false")) multiplexer_1 (
    .in0({32{1'b1}}), .in1(not_1_out), .out(multiplexer_1_out), .sel(RESET));
  assign not_1_out = ~32'h435021;  // NOT_Gate not_1, 32 bits wide
  assign not_2_out = ~4'b0001;  // NOT_Gate not_2, 4 bits wide
  Multiplexer #(.width(4), .enable("false")) multiplexer_2 (
    .in0(4'b1111), .in1(not_2_out), .out(multiplexer_2_out), .sel(RESET));
  Multiplexer #(.width(32), .enable("false")) multiplexer_3 (
    .in0({32{1'b1}}), .in1(32'h435021), .out(multiplexer_3_out), .sel(RESET));
  Multiplexer #(.width(4), .enable("false")) multiplexer_4 (
    .in0(4'b1111), .in1(4'b0001), .out(multiplexer_4_out), .sel(RESET));
  Register_32_bits_Des register_32_bits_des_1 (
    .Entrada(Entrada_32), .CLK(CLK), .Salida({Addr, JAM, ALU, C, Mem}), .nPRE(multiplexer_1_out),
    .nCLR(multiplexer_3_out));
  Register_4_bits_Des register_4_bits_des_1 (
    .Entrada(Entrada_4), .CLK(CLK), .Salida(B), .nPRE(multiplexer_2_out), .nCLR(multiplexer_4_out));
endmodule

module Data_Path (
  input  MAR_C,
  input  [31:0] MEM_RD,
  input  MDR_B,
  input  MDR_C,
  input  rd,
  input  [7:0] MEM_FETCH,
  input  PC_B,
  input  PC_C,
  input  MBR,
  input  fetch,
  input  MBRU,
  input  SP_B,
  input  SP_C,
  input  LV_B,
  input  LV_C,
  input  CPP_B,
  input  CPP_C,
  input  RESET,
  input  TOS_B,
  input  TOS_C,
  input  OPC_B,
  input  OPC_C,
  input  H_C,
  input  INVA,
  input  ENA,
  input  CLK,
  input  ENB,
  input  INC,
  input  [1:0] F,
  input  SRA1,
  input  SLL8,
  output [31:0] MEM_WR,
  output [31:0] MEM_MAR,
  output [31:0] MEM_PC,
  output [7:0] OP_CODE,
  output [31:0] B,
  output N,
  output Z,
  output [31:0] C
);

  wire undriven;
  wire [7:0] multiplexer_1_out;
  wire [31:0] alu_32_bits_1_salida, multiplexer_2_out;

  Multiplexer #(.width(8), .enable("false")) multiplexer_1 (
    .in0({8{1'b1}}), .in1({8{1'b0}}), .out(multiplexer_1_out), .sel(RESET));
  Multiplexer #(.width(32), .enable("false")) multiplexer_2 (
    .in0({32{1'b1}}), .in1({32{1'b0}}), .out(multiplexer_2_out), .sel(RESET));
  Multiplexer #(.width(32), .enable("false")) multiplexer_3 (.in0(C), .in1(MEM_RD), .sel(rd));  // open: out
  assign B = MDR_B ? MEM_WR : 32'bz;  // Controlled_Buffer controlled_buffer_1
  assign B = PC_B ? MEM_PC : 32'bz;  // Controlled_Buffer controlled_buffer_2
  MBR_EN mbr_en_1 (.in_1(OP_CODE), .Salida_Signada(B), .Salida_No_Signada(B), .MRB(MBR), .MBRU(MBRU));
  Controlled_Buffer #(.width(32)) controlled_buffer_3 (.out(B), .en(SP_B));  // open: in
  Controlled_Buffer #(.width(32)) controlled_buffer_4 (.out(B), .en(LV_B));  // open: in
  Controlled_Buffer #(.width(32)) controlled_buffer_5 (.out(B), .en(CPP_B));  // open: in
  Controlled_Buffer #(.width(32)) controlled_buffer_6 (.out(B), .en(TOS_B));  // open: in
  Controlled_Buffer #(.width(32)) controlled_buffer_7 (.out(B), .en(OPC_B));  // open: in
  BARREL_SHIFTER_32BIT barrel_shifter_32bit_1 (
    .CH2(SLL8), .CH1(SRA1), .L_R(undriven), ._0(alu_32_bits_1_salida[0]), ._1(alu_32_bits_1_salida[1]),
    ._2(alu_32_bits_1_salida[2]), ._3(alu_32_bits_1_salida[3]), ._4(alu_32_bits_1_salida[4]),
    ._5(alu_32_bits_1_salida[5]), ._6(alu_32_bits_1_salida[6]), ._7(alu_32_bits_1_salida[7]),
    ._8(alu_32_bits_1_salida[8]), ._9(alu_32_bits_1_salida[9]), ._10(alu_32_bits_1_salida[10]),
    ._11(alu_32_bits_1_salida[11]), ._12(alu_32_bits_1_salida[12]), ._13(alu_32_bits_1_salida[13]),
    ._14(alu_32_bits_1_salida[14]), ._15(alu_32_bits_1_salida[15]), ._16(alu_32_bits_1_salida[16]),
    ._17(alu_32_bits_1_salida[17]), ._18(alu_32_bits_1_salida[18]), ._19(alu_32_bits_1_salida[19]),
    ._20(alu_32_bits_1_salida[20]), ._21(alu_32_bits_1_salida[21]), ._22(alu_32_bits_1_salida[22]),
    ._23(alu_32_bits_1_salida[23]), ._24(alu_32_bits_1_salida[24]), ._25(alu_32_bits_1_salida[25]),
    ._26(alu_32_bits_1_salida[26]), ._27(alu_32_bits_1_salida[27]), ._28(alu_32_bits_1_salida[28]),
    ._29(alu_32_bits_1_salida[29]), ._30(alu_32_bits_1_salida[30]), ._31(alu_32_bits_1_salida[31]));  // open: _0_2, _1_2, _2_2, _3_2, _4_2, _5_2, _6_2, _7_2, _8_2, _9_2, _10_2, _11_2, _12_2, _13_2, _14_2, _15_2, _16_2, _17_2, _18_2, _19_2, _20_2, _21_2, _22_2, _23_2, _24_2, _25_2, _26_2, _27_2, _28_2, _29_2, _30_2, _31_2
  Alu_32_bits alu_32_bits_1 (
    .B(B), .Cin(INC), .INVA(ENA), .ENB(ENB), .F(F), .Salida(alu_32_bits_1_salida), .Cout(N));  // open: A, ENA

  assign Z = N;

  // Notes on the sheet:
  //   Preset 8 Bits
  //   Clear 8 Bits
  //   Preset 32 Bits
  //   Clear 32 Bits
  //   Bus B
  //   Bus C
endmodule

module Register_32_bits_Hold___Paralel_Load (
  input  [31:0] nPRE,
  input  [31:0] Entrada,
  input  LOAD,
  input  CLK,
  input  [31:0] nCLR,
  output [31:0] Salida
);

  wire [7:0] multiplexer_1_out_2;
  wire [23:0] multiplexer_1_out;

  Multiplexer #(.width(32), .enable("false")) multiplexer_1 (
    .in1(Entrada), .out({multiplexer_1_out_2, multiplexer_1_out}), .sel(LOAD));  // open: in0
  Register_8_bits_Hold___Paralel_Load register_8_bits_hold_paralel_load_1 (
    .Entrada(multiplexer_1_out[7:0]), .LOAD(LOAD), .CLK(CLK), .Salida(Salida[7:0]), .nPRE(nPRE[7:0]),
    .nCLR(nCLR[7:0]));
  Register_8_bits_Hold___Paralel_Load register_8_bits_hold_paralel_load_2 (
    .Entrada(multiplexer_1_out[15:8]), .LOAD(LOAD), .CLK(CLK), .Salida(Salida[15:8]), .nPRE(nPRE[15:8]),
    .nCLR(nCLR[15:8]));
  Register_8_bits_Hold___Paralel_Load register_8_bits_hold_paralel_load_3 (
    .Entrada(multiplexer_1_out[23:16]), .LOAD(LOAD), .CLK(CLK), .Salida(Salida[23:16]), .nPRE(nPRE[23:16]),
    .nCLR(nCLR[23:16]));
  Register_8_bits_Hold___Paralel_Load register_8_bits_hold_paralel_load_4 (
    .Entrada(multiplexer_1_out_2), .LOAD(LOAD), .CLK(CLK), .Salida(Salida[31:24]), .nPRE(nPRE[31:24]),
    .nCLR(nCLR[31:24]));
endmodule

module Register_32_bits_Des (
  input  [31:0] nPRE,
  input  [31:0] Entrada,
  input  CLK,
  input  [31:0] nCLR,
  output [31:0] Salida
);

  D_FlipFlop_Des d_flipflop_des_1 (
    .D(Entrada[31]), .CLK(CLK), .Q(Salida[31]), .nPRE(nPRE[31]), .nCLR(nCLR[31]));  // open: nQ
  D_FlipFlop_Des d_flipflop_des_2 (
    .D(Entrada[30]), .CLK(CLK), .Q(Salida[30]), .nPRE(nPRE[30]), .nCLR(nCLR[30]));  // open: nQ
  D_FlipFlop_Des d_flipflop_des_3 (
    .D(Entrada[29]), .CLK(CLK), .Q(Salida[29]), .nPRE(nPRE[29]), .nCLR(nCLR[29]));  // open: nQ
  D_FlipFlop_Des d_flipflop_des_4 (
    .D(Entrada[28]), .CLK(CLK), .Q(Salida[28]), .nPRE(nPRE[28]), .nCLR(nCLR[28]));  // open: nQ
  D_FlipFlop_Des d_flipflop_des_5 (
    .D(Entrada[27]), .CLK(CLK), .Q(Salida[27]), .nPRE(nPRE[27]), .nCLR(nCLR[27]));  // open: nQ
  D_FlipFlop_Des d_flipflop_des_6 (
    .D(Entrada[26]), .CLK(CLK), .Q(Salida[26]), .nPRE(nPRE[26]), .nCLR(nCLR[26]));  // open: nQ
  D_FlipFlop_Des d_flipflop_des_7 (
    .D(Entrada[25]), .CLK(CLK), .Q(Salida[25]), .nPRE(nPRE[25]), .nCLR(nCLR[25]));  // open: nQ
  D_FlipFlop_Des d_flipflop_des_8 (
    .D(Entrada[24]), .CLK(CLK), .Q(Salida[24]), .nPRE(nPRE[24]), .nCLR(nCLR[24]));  // open: nQ
  D_FlipFlop_Des d_flipflop_des_9 (
    .D(Entrada[23]), .CLK(CLK), .Q(Salida[23]), .nPRE(nPRE[23]), .nCLR(nCLR[23]));  // open: nQ
  D_FlipFlop_Des d_flipflop_des_10 (
    .D(Entrada[22]), .CLK(CLK), .Q(Salida[22]), .nPRE(nPRE[22]), .nCLR(nCLR[22]));  // open: nQ
  D_FlipFlop_Des d_flipflop_des_11 (
    .D(Entrada[21]), .CLK(CLK), .Q(Salida[21]), .nPRE(nPRE[21]), .nCLR(nCLR[21]));  // open: nQ
  D_FlipFlop_Des d_flipflop_des_12 (
    .D(Entrada[20]), .CLK(CLK), .Q(Salida[20]), .nPRE(nPRE[20]), .nCLR(nCLR[20]));  // open: nQ
  D_FlipFlop_Des d_flipflop_des_13 (
    .D(Entrada[19]), .CLK(CLK), .Q(Salida[19]), .nPRE(nPRE[19]), .nCLR(nCLR[19]));  // open: nQ
  D_FlipFlop_Des d_flipflop_des_14 (
    .D(Entrada[18]), .CLK(CLK), .Q(Salida[18]), .nPRE(nPRE[18]), .nCLR(nCLR[18]));  // open: nQ
  D_FlipFlop_Des d_flipflop_des_15 (
    .D(Entrada[17]), .CLK(CLK), .Q(Salida[17]), .nPRE(nPRE[17]), .nCLR(nCLR[17]));  // open: nQ
  D_FlipFlop_Des d_flipflop_des_16 (
    .D(Entrada[16]), .CLK(CLK), .Q(Salida[16]), .nPRE(nPRE[16]), .nCLR(nCLR[16]));  // open: nQ
  D_FlipFlop_Des d_flipflop_des_17 (
    .D(Entrada[15]), .CLK(CLK), .Q(Salida[15]), .nPRE(nPRE[15]), .nCLR(nCLR[15]));  // open: nQ
  D_FlipFlop_Des d_flipflop_des_18 (
    .D(Entrada[14]), .CLK(CLK), .Q(Salida[14]), .nPRE(nPRE[14]), .nCLR(nCLR[14]));  // open: nQ
  D_FlipFlop_Des d_flipflop_des_19 (
    .D(Entrada[13]), .CLK(CLK), .Q(Salida[13]), .nPRE(nPRE[13]), .nCLR(nCLR[13]));  // open: nQ
  D_FlipFlop_Des d_flipflop_des_20 (
    .D(Entrada[12]), .CLK(CLK), .Q(Salida[12]), .nPRE(nPRE[12]), .nCLR(nCLR[12]));  // open: nQ
  D_FlipFlop_Des d_flipflop_des_21 (
    .D(Entrada[11]), .CLK(CLK), .Q(Salida[11]), .nPRE(nPRE[11]), .nCLR(nCLR[11]));  // open: nQ
  D_FlipFlop_Des d_flipflop_des_22 (
    .D(Entrada[10]), .CLK(CLK), .Q(Salida[10]), .nPRE(nPRE[10]), .nCLR(nCLR[10]));  // open: nQ
  D_FlipFlop_Des d_flipflop_des_23 (
    .D(Entrada[9]), .CLK(CLK), .Q(Salida[9]), .nPRE(nPRE[9]), .nCLR(nCLR[9]));  // open: nQ
  D_FlipFlop_Des d_flipflop_des_24 (
    .D(Entrada[8]), .CLK(CLK), .Q(Salida[8]), .nPRE(nPRE[8]), .nCLR(nCLR[8]));  // open: nQ
  D_FlipFlop_Des d_flipflop_des_25 (
    .D(Entrada[7]), .CLK(CLK), .Q(Salida[7]), .nPRE(nPRE[7]), .nCLR(nCLR[7]));  // open: nQ
  D_FlipFlop_Des d_flipflop_des_26 (
    .D(Entrada[6]), .CLK(CLK), .Q(Salida[6]), .nPRE(nPRE[6]), .nCLR(nCLR[6]));  // open: nQ
  D_FlipFlop_Des d_flipflop_des_27 (
    .D(Entrada[5]), .CLK(CLK), .Q(Salida[5]), .nPRE(nPRE[5]), .nCLR(nCLR[5]));  // open: nQ
  D_FlipFlop_Des d_flipflop_des_28 (
    .D(Entrada[4]), .CLK(CLK), .Q(Salida[4]), .nPRE(nPRE[4]), .nCLR(nCLR[4]));  // open: nQ
  D_FlipFlop_Des d_flipflop_des_29 (
    .D(Entrada[3]), .CLK(CLK), .Q(Salida[3]), .nPRE(nPRE[3]), .nCLR(nCLR[3]));  // open: nQ
  D_FlipFlop_Des d_flipflop_des_30 (
    .D(Entrada[2]), .CLK(CLK), .Q(Salida[2]), .nPRE(nPRE[2]), .nCLR(nCLR[2]));  // open: nQ
  D_FlipFlop_Des d_flipflop_des_31 (
    .D(Entrada[1]), .CLK(CLK), .Q(Salida[1]), .nPRE(nPRE[1]), .nCLR(nCLR[1]));  // open: nQ
  D_FlipFlop_Des d_flipflop_des_32 (
    .D(Entrada[0]), .CLK(CLK), .Q(Salida[0]), .nPRE(nPRE[0]), .nCLR(nCLR[0]));  // open: nQ
endmodule

module Register_8_bits_Hold___Paralel_Load (
  input  [7:0] nPRE,
  input  [7:0] Entrada,
  input  LOAD,
  input  CLK,
  input  [7:0] nCLR,
  output [7:0] Salida
);

  wire [7:0] multiplexer_1_out;

  Multiplexer #(.width(8), .enable("false")) multiplexer_1 (
    .in0(Salida), .in1(Entrada), .out(multiplexer_1_out), .sel(LOAD));
  D_FlipFlop_Asc d_flipflop_asc_1 (
    .D(multiplexer_1_out[0]), .CLK(CLK), .Q(Salida[0]), .nPRE(nPRE[0]), .nCLR(nCLR[0]));  // open: nQ
  D_FlipFlop_Asc d_flipflop_asc_2 (
    .D(multiplexer_1_out[1]), .CLK(CLK), .Q(Salida[1]), .nPRE(nPRE[1]), .nCLR(nCLR[1]));  // open: nQ
  D_FlipFlop_Asc d_flipflop_asc_3 (
    .D(multiplexer_1_out[2]), .CLK(CLK), .Q(Salida[2]), .nPRE(nPRE[2]), .nCLR(nCLR[2]));  // open: nQ
  D_FlipFlop_Asc d_flipflop_asc_4 (
    .D(multiplexer_1_out[3]), .CLK(CLK), .Q(Salida[3]), .nPRE(nPRE[3]), .nCLR(nCLR[3]));  // open: nQ
  D_FlipFlop_Asc d_flipflop_asc_5 (
    .D(multiplexer_1_out[4]), .CLK(CLK), .Q(Salida[4]), .nPRE(nPRE[4]), .nCLR(nCLR[4]));  // open: nQ
  D_FlipFlop_Asc d_flipflop_asc_6 (
    .D(multiplexer_1_out[5]), .CLK(CLK), .Q(Salida[5]), .nPRE(nPRE[5]), .nCLR(nCLR[5]));  // open: nQ
  D_FlipFlop_Asc d_flipflop_asc_7 (
    .D(multiplexer_1_out[6]), .CLK(CLK), .Q(Salida[6]), .nPRE(nPRE[6]), .nCLR(nCLR[6]));  // open: nQ
  D_FlipFlop_Asc d_flipflop_asc_8 (
    .D(multiplexer_1_out[7]), .CLK(CLK), .Q(Salida[7]), .nPRE(nPRE[7]), .nCLR(nCLR[7]));  // open: nQ
endmodule

module Register_4_bits_Des (
  input  [3:0] nPRE,
  input  [3:0] Entrada,
  input  CLK,
  input  [3:0] nCLR,
  output [3:0] Salida
);

  D_FlipFlop_Des d_flipflop_des_1 (
    .D(Entrada[3]), .CLK(CLK), .Q(Salida[3]), .nPRE(nPRE[3]), .nCLR(nCLR[3]));  // open: nQ
  D_FlipFlop_Des d_flipflop_des_2 (
    .D(Entrada[2]), .CLK(CLK), .Q(Salida[2]), .nPRE(nPRE[2]), .nCLR(nCLR[2]));  // open: nQ
  D_FlipFlop_Des d_flipflop_des_3 (
    .D(Entrada[1]), .CLK(CLK), .Q(Salida[1]), .nPRE(nPRE[1]), .nCLR(nCLR[1]));  // open: nQ
  D_FlipFlop_Des d_flipflop_des_4 (
    .D(Entrada[0]), .CLK(CLK), .Q(Salida[0]), .nPRE(nPRE[0]), .nCLR(nCLR[0]));  // open: nQ

  // Notes on the sheet:
  //   Registro con entrada paralela y salida paralela
endmodule

module MBR_EN (
  input  [7:0] in_1,
  input  MRB,
  input  MBRU,
  output [31:0] Salida_Signada,
  output [31:0] Salida_No_Signada
);

  assign Salida_Signada = MRB ? {{25{in_1[7]}}, in_1[6:0]} : 32'bz;  // Controlled_Buffer controlled_buffer_1
  assign Salida_No_Signada = MBRU ? {{24{1'b0}}, in_1} : 32'bz;  // Controlled_Buffer controlled_buffer_2
endmodule

module D_FlipFlop_Des (
  input  nPRE,
  input  D,
  input  CLK,
  input  nCLR,
  output Q,
  output nQ
);

  wire d_latch_1_q, not_1_out;

  D_Latch d_latch_1 (.D(D), .CLK(CLK), .Q(d_latch_1_q), .nPRE(nPRE), .nCLR(nCLR));  // open: nQ
  not not_1 (not_1_out, CLK);
  D_Latch d_latch_2 (.D(d_latch_1_q), .CLK(not_1_out), .Q(Q), .nQ(nQ), .nPRE(nPRE), .nCLR(nCLR));

  // Notes on the sheet:
  //   FlipFlop D flanco Descendente
endmodule

module D_FlipFlop_Asc (
  input  nPRE,
  input  D,
  input  CLK,
  input  nCLR,
  output Q,
  output nQ
);

  wire d_latch_1_q, not_1_out;

  not not_1 (not_1_out, CLK);
  D_Latch d_latch_1 (.D(D), .CLK(not_1_out), .Q(d_latch_1_q), .nPRE(nPRE), .nCLR(nCLR));  // open: nQ
  D_Latch d_latch_2 (.D(d_latch_1_q), .CLK(CLK), .Q(Q), .nQ(nQ), .nPRE(nPRE), .nCLR(nCLR));

  // Notes on the sheet:
  //   Flip-Flop D flanco Ascendente
endmodule

module D_Latch (
  input  nPRE,
  input  D,
  input  CLK,
  input  nCLR,
  output Q,
  output nQ
);

  wire nand_1_out, nand_2_out, not_1_out;

  not not_1 (not_1_out, D);
  nand nand_1 (nand_1_out, D, CLK);
  nand nand_2 (nand_2_out, CLK, not_1_out);
  nand nand_3 (Q, nand_1_out, nPRE, nQ);
  nand nand_4 (nQ, Q, nCLR, nand_2_out);
endmodule

module ALU_1_bit (
  input  Cin,
  input  INVA,
  input  A,
  input  ENA,
  input  B,
  input  ENB,
  input  [1:0] F,
  output Salida,
  output Cout
);

  wire and_1_out, and_2_out, decoder_1_out_3, decoder_1_out_4, decoder_1_out_5, decoder_1_out_6,
       sumador_completo_alu_1_s, unidad_logica_alu_1_and, unidad_logica_alu_1_not, unidad_logica_alu_1_or,
       xor_1_out;

  and and_1 (and_1_out, A, ENA);
  and and_2 (and_2_out, B, ENB);
  xor xor_1 (xor_1_out, INVA, and_1_out);
  Decoder decoder_1 (
    .F0(F[0]), .F1(F[1]), .out_3(decoder_1_out_3), .out_4(decoder_1_out_4), .out_5(decoder_1_out_5),
    .out_6(decoder_1_out_6));
  Unidad_Logica__ALU unidad_logica_alu_1 (
    .A(xor_1_out), .B(and_2_out), .EN1(decoder_1_out_3), .EN2(decoder_1_out_4), .EN3(decoder_1_out_5),
    .AND(unidad_logica_alu_1_and), .OR(unidad_logica_alu_1_or), .NOT(unidad_logica_alu_1_not));
  Sumador_Completo__ALU sumador_completo_alu_1 (
    .A(xor_1_out), .B(and_2_out), .EN(decoder_1_out_6), .S(sumador_completo_alu_1_s), .Cin(Cin), .Cout(Cout));
  or or_1 (Salida, unidad_logica_alu_1_and, unidad_logica_alu_1_or, unidad_logica_alu_1_not, sumador_completo_alu_1_s);
endmodule

module Unidad_Logica__ALU (
  input  A,
  input  B,
  input  EN1,
  input  EN2,
  input  EN3,
  output AND,
  output OR,
  output NOT
);

  wire and_1_out, not_1_out, or_1_out;

  and and_1 (and_1_out, A, B);
  or or_1 (or_1_out, A, B);
  not not_1 (not_1_out, B);
  and and_2 (AND, and_1_out, EN1);
  and and_3 (OR, or_1_out, EN2);
  and and_4 (NOT, not_1_out, EN3);
endmodule

module Sumador_Completo__ALU (
  input  Cin,
  input  A,
  input  B,
  input  EN,
  output S,
  output Cout
);

  wire and_1_out, and_2_out, xor_1_out, xor_2_out;

  and and_1 (and_1_out, EN, B, A);
  xor xor_1 (xor_1_out, A, B);
  or or_1 (Cout, and_1_out, and_2_out);
  and and_2 (and_2_out, EN, xor_1_out, Cin);
  xor xor_2 (xor_2_out, Cin, xor_1_out);
  and and_3 (S, xor_2_out, EN);
endmodule

module Desplazador (
  input  [31:0] Entrada,
  input  SRA1,
  input  SLL8,
  output [31:0] Salida
);
endmodule

module Register_32_bits_Hold___Paralel_load_2 (
  input  [31:0] nPRE,
  input  [31:0] Entrada,
  input  LOAD,
  input  CLK,
  input  [31:0] nCLR,
  output [31:0] Salida
);

  wire [31:0] multiplexer_1_out;

  Multiplexer #(.width(32), .enable("false")) multiplexer_1 (
    .in1(Entrada), .out(multiplexer_1_out), .sel(LOAD));  // open: in0
  Register_8_bits_Hold___Paralel_Load register_8_bits_hold_paralel_load_1 (
    .Entrada(multiplexer_1_out[7:0]), .LOAD(LOAD), .CLK(CLK), .Salida(Salida[7:0]), .nPRE(nPRE[7:0]),
    .nCLR(nCLR[7:0]));
  Register_8_bits_Hold___Paralel_Load register_8_bits_hold_paralel_load_2 (
    .Entrada(multiplexer_1_out[15:8]), .LOAD(LOAD), .CLK(CLK), .Salida(Salida[15:8]), .nPRE(nPRE[15:8]),
    .nCLR(nCLR[15:8]));
  Register_8_bits_Hold___Paralel_Load register_8_bits_hold_paralel_load_3 (
    .Entrada(multiplexer_1_out[23:16]), .LOAD(LOAD), .CLK(CLK), .Salida(Salida[23:16]), .nPRE(nPRE[23:16]),
    .nCLR(nCLR[23:16]));
  Register_8_bits_Hold___Paralel_Load register_8_bits_hold_paralel_load_4 (
    .Entrada(multiplexer_1_out[31:24]), .LOAD(LOAD), .CLK(CLK), .Salida(Salida[31:24]), .nPRE(nPRE[31:24]),
    .nCLR(nCLR[31:24]));
endmodule

// Deco
module Decoder (
  input  F0,
  input  F1,
  output out_3,
  output out_4,
  output out_5,
  output out_6
);

  wire not_1_out, not_2_out, not_3_out, not_4_out;

  not not_1 (not_1_out, F0);
  not not_2 (not_2_out, F1);
  not not_3 (not_3_out, F0);
  not not_4 (not_4_out, F1);
  and and_1 (out_3, not_1_out, not_2_out);
  and and_2 (out_4, not_3_out, F1);
  and and_3 (out_5, F0, not_4_out);
  and and_4 (out_6, F0, F1);
endmodule

module Alu_8_bits (
  input  [7:0] B,
  input  [7:0] A,
  input  Cin,
  input  INVA,
  input  ENA,
  input  ENB,
  input  [1:0] F,
  output [7:0] Salida,
  output Cout
);

  wire alu_1_bit_1_cout, alu_1_bit_2_cout, alu_1_bit_3_cout, alu_1_bit_4_cout, alu_1_bit_5_cout,
       alu_1_bit_6_cout, alu_1_bit_7_cout;

  ALU_1_bit alu_1_bit_1 (
    .INVA(INVA), .A(A[0]), .ENA(ENA), .B(B[0]), .ENB(ENB), .F(F), .Salida(Salida[0]), .Cin(Cin),
    .Cout(alu_1_bit_1_cout));
  ALU_1_bit alu_1_bit_2 (
    .INVA(INVA), .A(A[1]), .ENA(ENA), .B(B[1]), .ENB(ENB), .F(F), .Salida(Salida[1]), .Cin(alu_1_bit_1_cout),
    .Cout(alu_1_bit_2_cout));
  ALU_1_bit alu_1_bit_3 (
    .INVA(INVA), .A(A[2]), .ENA(ENA), .B(B[2]), .ENB(ENB), .F(F), .Salida(Salida[2]), .Cin(alu_1_bit_2_cout),
    .Cout(alu_1_bit_3_cout));
  ALU_1_bit alu_1_bit_4 (
    .INVA(INVA), .A(A[3]), .ENA(ENA), .B(B[3]), .ENB(ENB), .F(F), .Salida(Salida[3]), .Cin(alu_1_bit_3_cout),
    .Cout(alu_1_bit_4_cout));
  ALU_1_bit alu_1_bit_5 (
    .INVA(INVA), .A(A[4]), .ENA(ENA), .B(B[4]), .ENB(ENB), .F(F), .Salida(Salida[4]), .Cin(alu_1_bit_4_cout),
    .Cout(alu_1_bit_5_cout));
  ALU_1_bit alu_1_bit_6 (
    .INVA(INVA), .A(A[5]), .ENA(ENA), .B(B[5]), .ENB(ENB), .F(F), .Salida(Salida[5]), .Cin(alu_1_bit_5_cout),
    .Cout(alu_1_bit_6_cout));
  ALU_1_bit alu_1_bit_7 (
    .INVA(INVA), .A(A[6]), .ENA(ENA), .B(B[6]), .ENB(ENB), .F(F), .Salida(Salida[6]), .Cin(alu_1_bit_6_cout),
    .Cout(alu_1_bit_7_cout));
  ALU_1_bit alu_1_bit_8 (
    .INVA(INVA), .A(A[7]), .ENA(ENA), .B(B[7]), .ENB(ENB), .F(F), .Salida(Salida[7]), .Cin(alu_1_bit_7_cout),
    .Cout(Cout));
endmodule

// ALU
module Alu_32_bits (
  input  [31:0] A,
  input  [31:0] B,
  input  Cin,
  input  INVA,
  input  ENA,
  input  ENB,
  input  [1:0] F,
  output [31:0] Salida,
  output Cout
);

  wire alu_8_bits_1_cout, alu_8_bits_2_cout, alu_8_bits_3_cout;

  Alu_8_bits alu_8_bits_1 (
    .B(B[7:0]), .A(A[7:0]), .Cin(Cin), .INVA(INVA), .ENA(ENA), .ENB(ENB), .F(F), .Salida(Salida[7:0]),
    .Cout(alu_8_bits_1_cout));
  Alu_8_bits alu_8_bits_2 (
    .B(B[15:8]), .A(A[15:8]), .Cin(alu_8_bits_1_cout), .INVA(INVA), .ENA(ENA), .ENB(ENB), .F(F),
    .Salida(Salida[15:8]), .Cout(alu_8_bits_2_cout));
  Alu_8_bits alu_8_bits_3 (
    .B(B[23:16]), .A(A[23:16]), .Cin(alu_8_bits_2_cout), .INVA(INVA), .ENA(ENA), .ENB(ENB), .F(F),
    .Salida(Salida[23:16]), .Cout(alu_8_bits_3_cout));
  Alu_8_bits alu_8_bits_4 (
    .B(B[31:24]), .A(A[31:24]), .Cin(alu_8_bits_3_cout), .INVA(INVA), .ENA(ENA), .ENB(ENB), .F(F),
    .Salida(Salida[31:24]), .Cout(Cout));
endmodule

module SHIFTER_8BITS (
  input  _0,
  input  _1,
  input  _2,
  input  _3,
  input  _4,
  input  _5,
  input  _6,
  input  _7,
  input  Direccion,
  output _0_2,
  output _1_2,
  output _2_2,
  output _3_2,
  output _4_2,
  output _5_2,
  output _6_2,
  output _7_2
);

  wire and_1_out, and_3_out, and_4_out, and_5_out, and_6_out, and_7_out, and_8_out, and_9_out, and_10_out,
       and_11_out, and_12_out, and_14_out, not_1_out;

  not not_1 (not_1_out, Direccion);
  and and_1 (and_1_out, _0, Direccion);
  and and_2 (_0_2, not_1_out, _1);
  and and_3 (and_3_out, _1, Direccion);
  or or_1 (_1_2, and_1_out, and_4_out);
  and and_4 (and_4_out, not_1_out, _2);
  or or_2 (_2_2, and_3_out, and_6_out);
  and and_5 (and_5_out, _2, Direccion);
  and and_6 (and_6_out, not_1_out, _3);
  and and_7 (and_7_out, _3, Direccion);
  or or_3 (_3_2, and_5_out, and_8_out);
  and and_8 (and_8_out, not_1_out, _4);
  and and_9 (and_9_out, _4, Direccion);
  or or_4 (_4_2, and_7_out, and_10_out);
  and and_10 (and_10_out, not_1_out, _5);
  and and_11 (and_11_out, _5, Direccion);
  or or_5 (_5_2, and_9_out, and_12_out);
  and and_12 (and_12_out, not_1_out, _6);
  and and_13 (_7_2, _6, Direccion);
  or or_6 (_6_2, and_11_out, and_14_out);
  and and_14 (and_14_out, not_1_out, _7);

  // Notes on the sheet:
  //   0 = izquierda
  //   1 = derecha
endmodule

module SHIFTER_32BITS (
  input  _0,
  input  _1,
  input  _2,
  input  _3,
  input  _4,
  input  _5,
  input  _6,
  input  _7,
  input  _8,
  input  _9,
  input  _10,
  input  _11,
  input  _12,
  input  _13,
  input  _14,
  input  _15,
  input  _16,
  input  _17,
  input  _18,
  input  _19,
  input  _20,
  input  _21,
  input  _22,
  input  _23,
  input  _24,
  input  _25,
  input  _26,
  input  _27,
  input  _28,
  input  _29,
  input  _30,
  input  _31,
  input  Direccion,
  output _0_2,
  output _1_2,
  output _2_2,
  output _3_2,
  output _4_2,
  output _5_2,
  output _6_2,
  output _7_2,
  output _8_2,
  output _9_2,
  output _10_2,
  output _11_2,
  output _12_2,
  output _13_2,
  output _14_2,
  output _15_2,
  output _16_2,
  output _17_2,
  output _18_2,
  output _19_2,
  output _20_2,
  output _21_2,
  output _22_2,
  output _23_2,
  output _24_2,
  output _25_2,
  output _26_2,
  output _27_2,
  output _28_2,
  output _29_2,
  output _30_2,
  output _31_2
);

  wire and_1_out, and_3_out, and_4_out, and_5_out, and_6_out, and_7_out, and_8_out, and_9_out, and_10_out,
       and_11_out, and_12_out, and_13_out, and_14_out, and_15_out, and_16_out, and_17_out, and_18_out,
       and_19_out, and_20_out, and_21_out, and_22_out, and_23_out, and_24_out, and_25_out, and_26_out,
       and_27_out, and_28_out, and_29_out, and_30_out, and_31_out, and_32_out, and_33_out, and_34_out,
       and_35_out, and_36_out, and_37_out, and_38_out, and_39_out, and_40_out, and_41_out, and_42_out,
       and_43_out, and_44_out, and_45_out, and_46_out, and_47_out, and_48_out, and_49_out, and_50_out,
       and_51_out, and_52_out, and_53_out, and_54_out, and_55_out, and_56_out, and_57_out, and_58_out,
       and_59_out, and_60_out, and_61_out, not_1_out;

  not not_1 (not_1_out, Direccion);
  and and_1 (and_1_out, _0, Direccion);
  and and_2 (_0_2, not_1_out, _1);
  and and_3 (and_3_out, _1, Direccion);
  or or_1 (_1_2, and_1_out, and_4_out);
  and and_4 (and_4_out, not_1_out, _2);
  and and_5 (and_5_out, _2, Direccion);
  or or_2 (_2_2, and_3_out, and_6_out);
  and and_6 (and_6_out, not_1_out, _3);
  or or_3 (_3_2, and_5_out, and_9_out);
  and and_7 (and_7_out, _3, Direccion);
  and and_8 (and_8_out, _4, Direccion);
  and and_9 (and_9_out, not_1_out, _4);
  or or_4 (_4_2, and_7_out, and_10_out);
  and and_10 (and_10_out, not_1_out, _5);
  and and_11 (and_11_out, _5, Direccion);
  or or_5 (_5_2, and_8_out, and_12_out);
  and and_12 (and_12_out, not_1_out, _6);
  or or_6 (_6_2, and_11_out, and_14_out);
  and and_13 (and_13_out, _6, Direccion);
  and and_14 (and_14_out, not_1_out, _7);
  and and_15 (and_15_out, _7, Direccion);
  or or_7 (_7_2, and_13_out, and_16_out);
  and and_16 (and_16_out, not_1_out, _8);
  and and_17 (and_17_out, _8, Direccion);
  or or_8 (_8_2, and_15_out, and_19_out);
  and and_18 (and_18_out, _9, Direccion);
  and and_19 (and_19_out, not_1_out, _9);
  or or_9 (_9_2, and_17_out, and_20_out);
  and and_20 (and_20_out, not_1_out, _10);
  and and_21 (and_21_out, _10, Direccion);
  or or_10 (_10_2, and_18_out, and_22_out);
  and and_22 (and_22_out, not_1_out, _11);
  or or_11 (_11_2, and_21_out, and_25_out);
  and and_23 (and_23_out, _11, Direccion);
  and and_24 (and_24_out, _12, Direccion);
  and and_25 (and_25_out, not_1_out, _12);
  or or_12 (_12_2, and_23_out, and_26_out);
  and and_26 (and_26_out, not_1_out, _13);
  and and_27 (and_27_out, _13, Direccion);
  or or_13 (_13_2, and_24_out, and_28_out);
  and and_28 (and_28_out, not_1_out, _14);
  or or_14 (_14_2, and_27_out, and_29_out);
  and and_29 (and_29_out, not_1_out, _15);
  and and_30 (and_30_out, _14, Direccion);
  and and_31 (and_31_out, _15, Direccion);
  or or_15 (_15_2, and_30_out, and_32_out);
  and and_32 (and_32_out, not_1_out, _16);
  and and_33 (and_33_out, _16, Direccion);
  or or_16 (_16_2, and_31_out, and_34_out);
  and and_34 (and_34_out, not_1_out, _17);
  and and_35 (and_35_out, _17, Direccion);
  or or_17 (_17_2, and_33_out, and_36_out);
  and and_36 (and_36_out, not_1_out, _18);
  and and_37 (and_37_out, _18, Direccion);
  or or_18 (_18_2, and_35_out, and_38_out);
  and and_38 (and_38_out, not_1_out, _19);
  or or_19 (_19_2, and_37_out, and_41_out);
  and and_39 (and_39_out, _19, Direccion);
  and and_40 (and_40_out, _20, Direccion);
  and and_41 (and_41_out, not_1_out, _20);
  or or_20 (_20_2, and_39_out, and_42_out);
  and and_42 (and_42_out, not_1_out, _21);
  and and_43 (and_43_out, _21, Direccion);
  or or_21 (_21_2, and_40_out, and_44_out);
  and and_44 (and_44_out, not_1_out, _22);
  or or_22 (_22_2, and_43_out, and_46_out);
  and and_45 (and_45_out, _22, Direccion);
  and and_46 (and_46_out, not_1_out, _23);
  and and_47 (and_47_out, _23, Direccion);
  or or_23 (_23_2, and_45_out, and_48_out);
  and and_48 (and_48_out, not_1_out, _24);
  and and_49 (and_49_out, _24, Direccion);
  or or_24 (_24_2, and_47_out, and_50_out);
  and and_50 (and_50_out, not_1_out, _25);
  and and_51 (and_51_out, _25, Direccion);
  or or_25 (_25_2, and_49_out, and_52_out);
  and and_52 (and_52_out, not_1_out, _26);
  and and_53 (and_53_out, _26, Direccion);
  or or_26 (_26_2, and_51_out, and_54_out);
  and and_54 (and_54_out, not_1_out, _27);
  or or_27 (_27_2, and_53_out, and_56_out);
  and and_55 (and_55_out, _27, Direccion);
  and and_56 (and_56_out, not_1_out, _28);
  and and_57 (and_57_out, _28, Direccion);
  or or_28 (_28_2, and_55_out, and_58_out);
  and and_58 (and_58_out, not_1_out, _29);
  and and_59 (and_59_out, _29, Direccion);
  or or_29 (_29_2, and_57_out, and_60_out);
  and and_60 (and_60_out, not_1_out, _30);
  or or_30 (_30_2, and_59_out, and_61_out);
  and and_61 (and_61_out, not_1_out, _31);
  and and_62 (_31_2, _30, Direccion);

  // Notes on the sheet:
  //   0 = izquierda
  //   1 = derecha
endmodule

module SHIFTER_4BITS (
  input  _0,
  input  _1,
  input  _2,
  input  _3,
  input  _4,
  input  Direccion,
  output _0_2,
  output _1_2,
  output _2_2,
  output _3_2,
  output _4_2
);

  wire and_1_out, and_3_out, and_4_out, and_5_out, and_6_out, and_8_out, not_1_out;

  not not_1 (not_1_out, Direccion);
  and and_1 (and_1_out, _0, Direccion);
  and and_2 (_0_2, not_1_out, _1);
  and and_3 (and_3_out, _1, Direccion);
  or or_1 (_1_2, and_1_out, and_4_out);
  and and_4 (and_4_out, not_1_out, _2);
  or or_2 (_2_2, and_3_out, and_6_out);
  and and_5 (and_5_out, _2, Direccion);
  and and_6 (and_6_out, not_1_out, _3);
  and and_7 (_4_2, _3, Direccion);
  or or_3 (_3_2, and_5_out, and_8_out);
  and and_8 (and_8_out, not_1_out, _4);

  // Notes on the sheet:
  //   0 = izquierda
  //   1 = derecha
endmodule

module BARREL_SHIFTER_8BIT (
  input  _0,
  input  _0_2,
  input  _1,
  input  _2,
  input  _3,
  input  _4,
  input  _5,
  input  _6,
  input  _7,
  input  CH3,
  input  CH2,
  input  CH1,
  output _0_3,
  output _1_2,
  output _2_2,
  output _3_2,
  output _4_2,
  output _5_2,
  output _6_2,
  output _7_2
);

  wire multiplexer_1_out, multiplexer_2_out, multiplexer_5_out, multiplexer_6_out, multiplexer_7_out,
       multiplexer_8_out, multiplexer_10_out, multiplexer_11_out, multiplexer_13_out, multiplexer_14_out,
       multiplexer_17_out, multiplexer_18_out, multiplexer_19_out, multiplexer_20_out, multiplexer_22_out,
       multiplexer_23_out, not_1_out, not_2_out, not_3_out;

  not not_1 (not_1_out, CH1);
  not not_2 (not_2_out, CH3);
  not not_3 (not_3_out, CH2);
  Multiplexer #(.enable("false")) multiplexer_1 (.in0(_0), .in1(_0_2), .out(multiplexer_1_out), .sel(not_1_out));
  Multiplexer #(.enable("false")) multiplexer_2 (
    .in0(_0), .in1(multiplexer_1_out), .out(multiplexer_2_out), .sel(not_3_out));
  Multiplexer #(.enable("false")) multiplexer_3 (.in0(_0), .in1(multiplexer_2_out), .out(_0_3), .sel(not_2_out));
  Multiplexer #(.enable("false")) multiplexer_4 (.in0(_0), .in1(multiplexer_6_out), .out(_1_2), .sel(not_2_out));
  Multiplexer #(.enable("false")) multiplexer_5 (.in0(_0_2), .in1(_1), .out(multiplexer_5_out), .sel(not_1_out));
  Multiplexer #(.enable("false")) multiplexer_6 (
    .in0(_0), .in1(multiplexer_5_out), .out(multiplexer_6_out), .sel(not_3_out));
  Multiplexer #(.enable("false")) multiplexer_7 (.in0(_1), .in1(_2), .out(multiplexer_7_out), .sel(not_1_out));
  Multiplexer #(.enable("false")) multiplexer_8 (
    .in0(multiplexer_1_out), .in1(multiplexer_7_out), .out(multiplexer_8_out), .sel(not_3_out));
  Multiplexer #(.enable("false")) multiplexer_9 (.in0(_0), .in1(multiplexer_8_out), .out(_2_2), .sel(not_2_out));
  Multiplexer #(.enable("false")) multiplexer_10 (.in0(_2), .in1(_3), .out(multiplexer_10_out), .sel(not_1_out));
  Multiplexer #(.enable("false")) multiplexer_11 (
    .in0(multiplexer_5_out), .in1(multiplexer_10_out), .out(multiplexer_11_out), .sel(not_3_out));
  Multiplexer #(.enable("false")) multiplexer_12 (.in0(_0), .in1(multiplexer_11_out), .out(_3_2), .sel(not_2_out));
  Multiplexer #(.enable("false")) multiplexer_13 (.in0(_3), .in1(_4), .out(multiplexer_13_out), .sel(not_1_out));
  Multiplexer #(.enable("false")) multiplexer_14 (
    .in0(multiplexer_7_out), .in1(multiplexer_13_out), .out(multiplexer_14_out), .sel(not_3_out));
  Multiplexer #(.enable("false")) multiplexer_15 (
    .in0(multiplexer_2_out), .in1(multiplexer_14_out), .out(_4_2), .sel(not_2_out));
  Multiplexer #(.enable("false")) multiplexer_16 (
    .in0(multiplexer_6_out), .in1(multiplexer_18_out), .out(_5_2), .sel(not_2_out));
  Multiplexer #(.enable("false")) multiplexer_17 (.in0(_4), .in1(_5), .out(multiplexer_17_out), .sel(not_1_out));
  Multiplexer #(.enable("false")) multiplexer_18 (
    .in0(multiplexer_10_out), .in1(multiplexer_17_out), .out(multiplexer_18_out), .sel(not_3_out));
  Multiplexer #(.enable("false")) multiplexer_19 (.in0(_5), .in1(_6), .out(multiplexer_19_out), .sel(not_1_out));
  Multiplexer #(.enable("false")) multiplexer_20 (
    .in0(multiplexer_13_out), .in1(multiplexer_19_out), .out(multiplexer_20_out), .sel(not_3_out));
  Multiplexer #(.enable("false")) multiplexer_21 (
    .in0(multiplexer_8_out), .in1(multiplexer_20_out), .out(_6_2), .sel(not_2_out));
  Multiplexer #(.enable("false")) multiplexer_22 (.in0(_6), .in1(_7), .out(multiplexer_22_out), .sel(not_1_out));
  Multiplexer #(.enable("false")) multiplexer_23 (
    .in0(multiplexer_17_out), .in1(multiplexer_22_out), .out(multiplexer_23_out), .sel(not_3_out));
  Multiplexer #(.enable("false")) multiplexer_24 (
    .in0(multiplexer_11_out), .in1(multiplexer_23_out), .out(_7_2), .sel(not_2_out));
endmodule

// SHIFTER_32BIT
module BARREL_SHIFTER_32BIT (
  input  L_R,
  input  _0,
  input  _1,
  input  _2,
  input  _3,
  input  _4,
  input  _5,
  input  _6,
  input  _7,
  input  _8,
  input  _9,
  input  _10,
  input  _11,
  input  _12,
  input  _13,
  input  _14,
  input  _15,
  input  _16,
  input  _17,
  input  _18,
  input  _19,
  input  _20,
  input  _21,
  input  _22,
  input  _23,
  input  _24,
  input  _25,
  input  _26,
  input  _27,
  input  _28,
  input  _29,
  input  _30,
  input  _31,
  input  CH2,
  input  CH1,
  output _0_2,
  output _1_2,
  output _2_2,
  output _3_2,
  output _4_2,
  output _5_2,
  output _6_2,
  output _7_2,
  output _8_2,
  output _9_2,
  output _10_2,
  output _11_2,
  output _12_2,
  output _13_2,
  output _14_2,
  output _15_2,
  output _16_2,
  output _17_2,
  output _18_2,
  output _19_2,
  output _20_2,
  output _21_2,
  output _22_2,
  output _23_2,
  output _24_2,
  output _25_2,
  output _26_2,
  output _27_2,
  output _28_2,
  output _29_2,
  output _30_2,
  output _31_2
);

  wire multiplexer_1_out, multiplexer_3_out, multiplexer_5_out, multiplexer_7_out, multiplexer_9_out,
       multiplexer_11_out, multiplexer_13_out, multiplexer_15_out, multiplexer_17_out, multiplexer_19_out,
       multiplexer_21_out, multiplexer_23_out, multiplexer_25_out, multiplexer_27_out, multiplexer_29_out,
       multiplexer_31_out, multiplexer_33_out, multiplexer_35_out, multiplexer_37_out, multiplexer_39_out,
       multiplexer_41_out, multiplexer_43_out, multiplexer_45_out, multiplexer_47_out, multiplexer_49_out,
       multiplexer_51_out, multiplexer_53_out, multiplexer_55_out, multiplexer_57_out, multiplexer_59_out,
       multiplexer_61_out, multiplexer_63_out, not_1_out, not_2_out;

  not not_1 (not_1_out, CH2);
  not not_2 (not_2_out, CH1);
  Multiplexer #(.enable("false")) multiplexer_1 (.in0(L_R), .in1(_0), .out(multiplexer_1_out), .sel(not_2_out));
  Multiplexer #(.enable("false")) multiplexer_2 (.in0(L_R), .in1(multiplexer_1_out), .out(_0_2), .sel(not_1_out));
  Multiplexer #(.enable("false")) multiplexer_3 (.in0(_0), .in1(_1), .out(multiplexer_3_out), .sel(not_2_out));
  Multiplexer #(.enable("false")) multiplexer_4 (.in0(L_R), .in1(multiplexer_3_out), .out(_1_2), .sel(not_1_out));
  Multiplexer #(.enable("false")) multiplexer_5 (.in0(_1), .in1(_2), .out(multiplexer_5_out), .sel(not_2_out));
  Multiplexer #(.enable("false")) multiplexer_6 (.in0(L_R), .in1(multiplexer_5_out), .out(_2_2), .sel(not_1_out));
  Multiplexer #(.enable("false")) multiplexer_7 (.in0(_2), .in1(_3), .out(multiplexer_7_out), .sel(not_2_out));
  Multiplexer #(.enable("false")) multiplexer_8 (.in0(L_R), .in1(multiplexer_7_out), .out(_3_2), .sel(not_1_out));
  Multiplexer #(.enable("false")) multiplexer_9 (.in0(_3), .in1(_4), .out(multiplexer_9_out), .sel(not_2_out));
  Multiplexer #(.enable("false")) multiplexer_10 (.in0(L_R), .in1(multiplexer_9_out), .out(_4_2), .sel(not_1_out));
  Multiplexer #(.enable("false")) multiplexer_11 (.in0(_4), .in1(_5), .out(multiplexer_11_out), .sel(not_2_out));
  Multiplexer #(.enable("false")) multiplexer_12 (.in0(L_R), .in1(multiplexer_11_out), .out(_5_2), .sel(not_1_out));
  Multiplexer #(.enable("false")) multiplexer_13 (.in0(_5), .in1(_6), .out(multiplexer_13_out), .sel(not_2_out));
  Multiplexer #(.enable("false")) multiplexer_14 (.in0(L_R), .in1(multiplexer_13_out), .out(_6_2), .sel(not_1_out));
  Multiplexer #(.enable("false")) multiplexer_15 (.in0(_6), .in1(_7), .out(multiplexer_15_out), .sel(not_2_out));
  Multiplexer #(.enable("false")) multiplexer_16 (.in0(L_R), .in1(multiplexer_15_out), .out(_7_2), .sel(not_1_out));
  Multiplexer #(.enable("false")) multiplexer_17 (.in0(_7), .in1(_8), .out(multiplexer_17_out), .sel(not_2_out));
  Multiplexer #(.enable("false")) multiplexer_18 (
    .in0(multiplexer_1_out), .in1(multiplexer_17_out), .out(_8_2), .sel(not_1_out));
  Multiplexer #(.enable("false")) multiplexer_19 (.in0(_8), .in1(_9), .out(multiplexer_19_out), .sel(not_2_out));
  Multiplexer #(.enable("false")) multiplexer_20 (
    .in0(multiplexer_3_out), .in1(multiplexer_19_out), .out(_9_2), .sel(not_1_out));
  Multiplexer #(.enable("false")) multiplexer_21 (.in0(_9), .in1(_10), .out(multiplexer_21_out), .sel(not_2_out));
  Multiplexer #(.enable("false")) multiplexer_22 (
    .in0(multiplexer_5_out), .in1(multiplexer_21_out), .out(_10_2), .sel(not_1_out));
  Multiplexer #(.enable("false")) multiplexer_23 (.in0(_10), .in1(_11), .out(multiplexer_23_out), .sel(not_2_out));
  Multiplexer #(.enable("false")) multiplexer_24 (
    .in0(multiplexer_7_out), .in1(multiplexer_23_out), .out(_11_2), .sel(not_1_out));
  Multiplexer #(.enable("false")) multiplexer_25 (.in0(_11), .in1(_12), .out(multiplexer_25_out), .sel(not_2_out));
  Multiplexer #(.enable("false")) multiplexer_26 (
    .in0(multiplexer_9_out), .in1(multiplexer_25_out), .out(_12_2), .sel(not_1_out));
  Multiplexer #(.enable("false")) multiplexer_27 (.in0(_12), .in1(_13), .out(multiplexer_27_out), .sel(not_2_out));
  Multiplexer #(.enable("false")) multiplexer_28 (
    .in0(multiplexer_11_out), .in1(multiplexer_27_out), .out(_13_2), .sel(not_1_out));
  Multiplexer #(.enable("false")) multiplexer_29 (.in0(_13), .in1(_14), .out(multiplexer_29_out), .sel(not_2_out));
  Multiplexer #(.enable("false")) multiplexer_30 (
    .in0(multiplexer_13_out), .in1(multiplexer_29_out), .out(_14_2), .sel(not_1_out));
  Multiplexer #(.enable("false")) multiplexer_31 (.in0(_14), .in1(_15), .out(multiplexer_31_out), .sel(not_2_out));
  Multiplexer #(.enable("false")) multiplexer_32 (
    .in0(multiplexer_15_out), .in1(multiplexer_31_out), .out(_15_2), .sel(not_1_out));
  Multiplexer #(.enable("false")) multiplexer_33 (.in0(_15), .in1(_16), .out(multiplexer_33_out), .sel(not_2_out));
  Multiplexer #(.enable("false")) multiplexer_34 (
    .in0(multiplexer_17_out), .in1(multiplexer_33_out), .out(_16_2), .sel(not_1_out));
  Multiplexer #(.enable("false")) multiplexer_35 (.in0(_16), .in1(_17), .out(multiplexer_35_out), .sel(not_2_out));
  Multiplexer #(.enable("false")) multiplexer_36 (
    .in0(multiplexer_19_out), .in1(multiplexer_35_out), .out(_17_2), .sel(not_1_out));
  Multiplexer #(.enable("false")) multiplexer_37 (.in0(_17), .in1(_18), .out(multiplexer_37_out), .sel(not_2_out));
  Multiplexer #(.enable("false")) multiplexer_38 (
    .in0(multiplexer_21_out), .in1(multiplexer_37_out), .out(_18_2), .sel(not_1_out));
  Multiplexer #(.enable("false")) multiplexer_39 (.in0(_18), .in1(_19), .out(multiplexer_39_out), .sel(not_2_out));
  Multiplexer #(.enable("false")) multiplexer_40 (
    .in0(multiplexer_23_out), .in1(multiplexer_39_out), .out(_19_2), .sel(not_1_out));
  Multiplexer #(.enable("false")) multiplexer_41 (.in0(_19), .in1(_20), .out(multiplexer_41_out), .sel(not_2_out));
  Multiplexer #(.enable("false")) multiplexer_42 (
    .in0(multiplexer_25_out), .in1(multiplexer_41_out), .out(_20_2), .sel(not_1_out));
  Multiplexer #(.enable("false")) multiplexer_43 (.in0(_20), .in1(_21), .out(multiplexer_43_out), .sel(not_2_out));
  Multiplexer #(.enable("false")) multiplexer_44 (
    .in0(multiplexer_27_out), .in1(multiplexer_43_out), .out(_21_2), .sel(not_1_out));
  Multiplexer #(.enable("false")) multiplexer_45 (.in0(_21), .in1(_22), .out(multiplexer_45_out), .sel(not_2_out));
  Multiplexer #(.enable("false")) multiplexer_46 (
    .in0(multiplexer_29_out), .in1(multiplexer_45_out), .out(_22_2), .sel(not_1_out));
  Multiplexer #(.enable("false")) multiplexer_47 (.in0(_22), .in1(_23), .out(multiplexer_47_out), .sel(not_2_out));
  Multiplexer #(.enable("false")) multiplexer_48 (
    .in0(multiplexer_31_out), .in1(multiplexer_47_out), .out(_23_2), .sel(not_1_out));
  Multiplexer #(.enable("false")) multiplexer_49 (.in0(_23), .in1(_24), .out(multiplexer_49_out), .sel(not_2_out));
  Multiplexer #(.enable("false")) multiplexer_50 (
    .in0(multiplexer_33_out), .in1(multiplexer_49_out), .out(_24_2), .sel(not_1_out));
  Multiplexer #(.enable("false")) multiplexer_51 (.in0(_24), .in1(_25), .out(multiplexer_51_out), .sel(not_2_out));
  Multiplexer #(.enable("false")) multiplexer_52 (
    .in0(multiplexer_35_out), .in1(multiplexer_51_out), .out(_25_2), .sel(not_1_out));
  Multiplexer #(.enable("false")) multiplexer_53 (.in0(_25), .in1(_26), .out(multiplexer_53_out), .sel(not_2_out));
  Multiplexer #(.enable("false")) multiplexer_54 (
    .in0(multiplexer_37_out), .in1(multiplexer_53_out), .out(_26_2), .sel(not_1_out));
  Multiplexer #(.enable("false")) multiplexer_55 (.in0(_26), .in1(_27), .out(multiplexer_55_out), .sel(not_2_out));
  Multiplexer #(.enable("false")) multiplexer_56 (
    .in0(multiplexer_39_out), .in1(multiplexer_55_out), .out(_27_2), .sel(not_1_out));
  Multiplexer #(.enable("false")) multiplexer_57 (.in0(_27), .in1(_28), .out(multiplexer_57_out), .sel(not_2_out));
  Multiplexer #(.enable("false")) multiplexer_58 (
    .in0(multiplexer_41_out), .in1(multiplexer_57_out), .out(_28_2), .sel(not_1_out));
  Multiplexer #(.enable("false")) multiplexer_59 (.in0(_28), .in1(_29), .out(multiplexer_59_out), .sel(not_2_out));
  Multiplexer #(.enable("false")) multiplexer_60 (
    .in0(multiplexer_43_out), .in1(multiplexer_59_out), .out(_29_2), .sel(not_1_out));
  Multiplexer #(.enable("false")) multiplexer_61 (.in0(_29), .in1(_30), .out(multiplexer_61_out), .sel(not_2_out));
  Multiplexer #(.enable("false")) multiplexer_62 (
    .in0(multiplexer_45_out), .in1(multiplexer_61_out), .out(_30_2), .sel(not_1_out));
  Multiplexer #(.enable("false")) multiplexer_63 (.in0(_30), .in1(_31), .out(multiplexer_63_out), .sel(not_2_out));
  Multiplexer #(.enable("false")) multiplexer_64 (
    .in0(multiplexer_47_out), .in1(multiplexer_63_out), .out(_31_2), .sel(not_1_out));
endmodule
